# Fritzing sketch mp2 (saved by Fritzing 0.9.3b)
breadboards: 1

parts:
  Raspberry_Pi = Raspberry Pi 2
  R2 = Resistor [tolerance=±5% resistance=51 package=THT]
  R3 = Resistor [tolerance=±5% resistance=10k package=THT]
  Arduino_promini = Arduino Pro Mini v13
  Motor_Driver = Motor Driver 1A Dual TB6612FNG
  LED_green = LED - 5mm [color="Green (565nm)" part_number="Status led 2" package="5 mm [THT]"]
  LED_yellow = LED - 5mm [color="Yellow (595nm)" part_number="Status led 1" package="5 mm [THT]"]
  Switch = Momentary Switch [part_number="First button" package=ksa_sealed_tac_switch]
  Switch_2 = Momentary Switch [part_number=shutdown package=ksa_sealed_tac_switch]
  LED_white = LED - 3mm [color="White (4500K)" part_number=Boot package="3 mm [THT]"]
  R1 = Resistor [tolerance=±5% resistance=51 package=THT]
  R4 = Resistor [tolerance=±5% resistance=100 package=THT]
  R5 = Resistor [tolerance=±5% resistance=10k package=THT]
  Servo_motor = Basic Servo [part_number=stopper]
  LED_white_2 = LED - 3mm [color="White (4500K)" part_number=Explode package="3 mm [THT]"]
  Switch_3 = SWITCH-MOMENTARY-2 [part_number="Second button" package=tactile-pth]
  LED_red = LED - 5mm [color="Red (633nm)" part_number=Siren package="5 mm [THT]"]
  R6 = Resistor [tolerance=±5% resistance=10 package=THT]
  R7 = Resistor [tolerance=±5% resistance=200 package=THT]
  R8 = Resistor [tolerance=±5% resistance=200 package=THT]
  R9 = Resistor [tolerance=±5% resistance=200 package=THT]
  R10 = Resistor [tolerance=±5% resistance=200 package=THT]
  R11 = Resistor [tolerance=±5% resistance=200 package=THT]
  LED_red_2 = LED - 5mm [color="Red (633nm)" part_number=FIre package="5 mm [THT]"]
  LED_red_3 = LED - 5mm [color="Red (633nm)" part_number=Fire package="5 mm [THT]"]
  LED_red_4 = LED - 5mm [color="Red (633nm)" part_number=Fire package="5 mm [THT]"]
  LED_red_5 = LED - 5mm [color="Red (633nm)" part_number=Fire package="5 mm [THT]"]
  LED_red_6 = LED - 5mm [color="Red (633nm)" part_number=Fire package="5 mm [THT]"]
  Switch_4 = Momentary Switch [part_number="LED on-off" package=ksa_sealed_tac_switch]
  Relay_switch = RELAY [package=relay-jzc]
  Electromagnet = Solenoid
  Battery = Battery Holders [package=battery-aa]
  Switch_5 = SPST Switch [part_number=Battery package=switche-dpdt]
  Motor1 = DC Motor [part_number="Destroy conveyor"]
  Motor2 = DC Motor [part_number="Move conveyor"]
  R12 = Resistor [tolerance=±5% resistance=10k package=THT]

nets:
  3V3: Raspberry_Pi.3v3, Raspberry_Pi.3V3, Motor_Driver.VCC, Motor_Driver.STBY
  N1: Raspberry_Pi.GPIO2, R2.Pin_1
  N2: Raspberry_Pi.GPIO3, Switch.4
  N3: Raspberry_Pi.GIPO4, R1.Pin_1
  N4: Raspberry_Pi.GIPO17, Motor_Driver.PWMA
  N5: Raspberry_Pi.GIPO27, Motor_Driver.AIN2
  N6: Raspberry_Pi.GIPO22, Motor_Driver.AIN1
  N7: Raspberry_Pi.GIPO10, Motor_Driver.BIN1
  N8: Raspberry_Pi.GIPO9, Motor_Driver.BIN2
  N9: Raspberry_Pi.GIPO11, Motor_Driver.PWMB
  GND: Raspberry_Pi.GND, R3.Pin_1, Arduino_promini.GND, Motor_Driver.GND, LED_green.cathode, LED_yellow.cathode, Switch.2, Switch_2.4, LED_white.cathode, Servo_motor.gnd, LED_white_2.cathode, Switch_3.2, LED_red.cathode, R7.Pin_1, R8.Pin_1, R9.Pin_1, R10.Pin_1, R11.Pin_1, Relay_switch.COIL1, Electromagnet.pin2, Switch_5.P, R12.Pin_1
  N10: Raspberry_Pi.ID_SD, R6.Pin_0
  N11: Raspberry_Pi.GIPO5, R4.Pin_0
  N12: Raspberry_Pi.GIPO13, R5.Pin_0
  N13: Raspberry_Pi.GIPO19, Switch_2.2
  N14: Raspberry_Pi.GIPO26, Relay_switch.COIL2
  N15: Raspberry_Pi.GIPO24, R3.Pin_0, Arduino_promini.D12/MISO
  N16: Raspberry_Pi.GIPO23, Servo_motor.pulse
  N17: Raspberry_Pi.GIPO18, Switch_3.1
  5V: Raspberry_Pi.5V, Arduino_promini.RAW, Servo_motor.vcc
  N18: R2.Pin_0, LED_yellow.anode
  N19: Arduino_promini.VCC, Switch_4.2
  N20: Arduino_promini.D4, Switch_4.4, R12.Pin_0
  N21: Arduino_promini.D2, LED_red_2.anode, LED_red_3.anode, LED_red_4.anode, LED_red_5.anode, LED_red_6.anode
  N22: Motor_Driver.B01, Motor2.pin_2
  N23: Motor_Driver.B02, Motor2.pin_1
  N24: Motor_Driver.A02, Motor1.pin_2
  N25: Motor_Driver.A01, Motor1.pin_1
  N26: Motor_Driver.VM, Relay_switch.MAIN, Battery.+
  N27: LED_green.anode, R1.Pin_0
  N28: LED_white.anode, R5.Pin_1
  N29: R4.Pin_1, LED_red.anode
  N30: LED_white_2.anode, R6.Pin_1
  N31: R7.Pin_0, LED_red_2.cathode
  N32: R8.Pin_0, LED_red_3.cathode
  N33: R9.Pin_0, LED_red_4.cathode
  N34: R10.Pin_0, LED_red_5.cathode
  N35: R11.Pin_0, LED_red_6.cathode
  N36: Relay_switch.NC, Electromagnet.pin1
  N37: Battery.-, Switch_5.S
